# Fritzing sketch FeurIO (saved by Fritzing 0.9.3b)
breadboards: 1

parts:
  R1 = Photocell (LDR) [package=THT]
  Bauteil1 = Arduino Micro (Rev3)
  R2 = Resistor [tolerance=±5% resistance=10k package=THT]
  IR1 = TSOP312.., 314.. [package=THT]
  T1 = LM35 Temperature Sensor [package="TO92 [THT]"]
  LED1 = SMD RGB LED (WS2812) [package=5050]
  LED2 = SMD RGB LED (WS2812) [package=5050]
  LED3 = SMD RGB LED (WS2812) [package=5050]
  LED4 = SMD RGB LED (WS2812) [package=5050]
  LED5 = SMD RGB LED (WS2812) [package=5050]
  LED6 = SMD RGB LED (WS2812) [package=5050]
  LED7 = SMD RGB LED (WS2812) [package=5050]
  Q1 = NPN-Transistor [package="TO92 [THT]"]
  M2 = DC Motor
  R3 = Resistor [tolerance=±5% resistance=220 package=THT]

nets:
  VCC: R1.pin_0, Bauteil1.5V, IR1.Vs, T1.+Vs, LED1.VCC, LED2.VCC, LED3.VCC, LED4.VCC
  N1: R1.pin_1, R2.Pin_0
  GND: Bauteil1.GND, R2.Pin_1, IR1.GND, T1.GND, LED1.DOut, LED2.DOut, LED3.DOut, LED4.DOut
  N2: LED1.NC, LED7.VCC
  N3: LED1.VDD, LED7.DIn
  N4: LED1.VSS, LED7.DOut
  N5: LED5.NC, LED6.VSS
  VDD: LED5.VDD, LED6.VDD
  N6: LED5.VSS, LED6.NC
  N7: LED6.DOut, LED7.VSS
  N8: LED6.DIn, LED7.VDD
  N9: LED6.VCC, LED7.NC
  N10: Q1.E, M2.pin_2
  N11: Q1.B, R3.Pin_1
  N12: Q1.C, M2.pin_1
